# Fritzing sketch imagen-1654216412612 (saved by Fritzing 0.9.9b)
breadboards: 1

parts:
  LED1 = LED - 5mm [color="Red (633nm)" current=0.030 package="5 mm [THT]"]
  R1 = Resistor [tolerance=±5% resistance=220 power=0.25 package=THT]
  R2 = Rotary Potentiometer (Large) [maximum_resistance=100kΩ package=THT]
  Componente3 = Arduino Uno (Rev3) - ICSP

nets:
  N1: LED1.cathode, R1.Pin_1
  N2: LED1.anode, Componente3.D3_PWM
  N3: R1.Pin_0, R2.leg2, Componente3.GND
  N4: R2.leg1, Componente3.5V
  N5: R2.wiper, Componente3.A0
